// Logisim project CU.circ as structural Verilog: 2 circuits, main circuit CU
module CU (
  input  [7:0] in_1,
  output [3:0] Address,
  output Stop,
  output out_4,
  output Add,
  output Sub,
  output Beq,
  output Bnq,
  output Ld1,
  output Ld2,
  output Str1,
  output Str2,
  output Prt,
  output Inp
);

  Decoder #(.select(4), .enable("false")) decoder_1 (
    .out0(Stop), .out1(out_4), .out2(Add), .out3(Sub), .out4(Beq), .out5(Bnq), .out6(Ld1), .out7(Ld2),
    .out8(Str1), .out9(Str2), .out10(Prt), .out11(Inp), .sel(in_1[7:4]));  // open: out12, out13, out14, out15

  assign Address = in_1[3:0];
endmodule

module DataRegisters (
  input  Clk,
  input  Rw,
  input  Which,
  input  [7:0] in_4,
  output [7:0] DataOutput,
  output Eq
);

  wire and_1_out, and_2_out, xnor_1_out, xnor_2_out, xnor_3_out, xnor_4_out, xnor_5_out, xnor_6_out,
       xnor_7_out, xnor_8_out;
  wire [7:0] byte_storage_1_o1, byte_storage_2_o1;

  xnor xnor_1 (xnor_1_out, byte_storage_2_o1[7], byte_storage_1_o1[7]);
  xnor xnor_2 (xnor_2_out, byte_storage_2_o1[6], byte_storage_1_o1[6]);
  and and_1 (and_1_out, Rw, ~Which);  // AND_Gate
  and and_2 (and_2_out, Rw, Which);
  xnor xnor_3 (xnor_3_out, byte_storage_2_o1[5], byte_storage_1_o1[5]);
  xnor xnor_4 (xnor_4_out, byte_storage_2_o1[4], byte_storage_1_o1[4]);
  byte_storage byte_storage_1 (
    .o2(byte_storage_1_o1[1]), .o3(byte_storage_1_o1[2]), .o1(byte_storage_1_o1[0]), .b8(in_4[7]),
    .b7(in_4[6]), .b6(in_4[5]), .b5(in_4[4]), .b4(in_4[3]), .b3(in_4[2]), .b2(in_4[1]), .b1(in_4[0]),
    .Enable(and_1_out), .Clock(Clk), .o4(byte_storage_1_o1[3]), .o5(byte_storage_1_o1[4]),
    .o6(byte_storage_1_o1[5]), .o7(byte_storage_1_o1[6]), .o8(byte_storage_1_o1[7]));
  byte_storage byte_storage_2 (
    .o2(byte_storage_2_o1[1]), .o3(byte_storage_2_o1[2]), .o1(byte_storage_2_o1[0]), .b8(in_4[7]),
    .b7(in_4[6]), .b6(in_4[5]), .b5(in_4[4]), .b4(in_4[3]), .b3(in_4[2]), .b2(in_4[1]), .b1(in_4[0]),
    .Enable(and_2_out), .Clock(Clk), .o4(byte_storage_2_o1[3]), .o5(byte_storage_2_o1[4]),
    .o6(byte_storage_2_o1[5]), .o7(byte_storage_2_o1[6]), .o8(byte_storage_2_o1[7]));
  xnor xnor_5 (xnor_5_out, byte_storage_2_o1[3], byte_storage_1_o1[3]);
  Multiplexer #(.width(8), .enable("false")) multiplexer_1 (
    .in0(byte_storage_1_o1), .in1(byte_storage_2_o1), .out(DataOutput), .sel(Which));
  xnor xnor_6 (xnor_6_out, byte_storage_2_o1[1], byte_storage_1_o1[1]);
  xnor xnor_7 (xnor_7_out, byte_storage_2_o1[2], byte_storage_1_o1[2]);
  xnor xnor_8 (xnor_8_out, byte_storage_2_o1[0], byte_storage_1_o1[0]);
  and and_3 (Eq, xnor_8_out, xnor_6_out, xnor_7_out, xnor_5_out, xnor_4_out, xnor_3_out, xnor_2_out, xnor_1_out);
endmodule
